// Digital circuit ALU.dig as structural Verilog
module ALU (
  input  [2:0] op,
  input  [7:0] a,
  input  [7:0] b,
  output [7:0] out
);

  wire [7:0] add_1_s, and_1_out, barrelshifter_1_out, barrelshifter_2_out, not_1_out, or_1_out, sub_1_s,
       xor_1_out;

  assign and_1_out = a & b;  // And and_1, 8 bits wide
  assign or_1_out = a | b;  // Or or_1, 8 bits wide
  assign xor_1_out = a ^ b;  // XOr xor_1, 8 bits wide
  Add #(.Bits(8)) add_1 (.a(a), .b(b), .c_i(1'b0), .s(add_1_s));  // open: c_o
  Sub #(.Bits(8)) sub_1 (.a(a), .b(b), .c_i(1'b0), .s(sub_1_s));  // open: c_o
  assign not_1_out = ~a;  // Not not_1, 8 bits wide
  BarrelShifter #(.Bits(8), .barrelSigned("true")) barrelshifter_1 (.in(a), .shift(b[4:0]), .out(barrelshifter_1_out));
  BarrelShifter #(.Bits(8), .barrelSigned("true"), .direction("right")) barrelshifter_2 (
    .in(a), .shift(b[4:0]), .out(barrelshifter_2_out));
  Multiplexer #(.Bits(8), .Selector_Bits(3)) multiplexer_1 (
    .sel(op), .in_0(add_1_s), .in_1(sub_1_s), .in_2(and_1_out), .in_3(or_1_out), .in_4(not_1_out),
    .in_5(xor_1_out), .in_6(barrelshifter_1_out), .in_7(barrelshifter_2_out), .out(out));
endmodule
