// Digital circuit PC.dig as structural Verilog
module PC (
  input  C,
  input  [7:0] Din,
  input  str,
  output [7:0] D
);

  wire [7:0] add_1_s, register_1_q;

  Register #(.Bits(8)) register_1 (.D(D), .C(C), .en(1'b1), .Q(register_1_q));
  Add #(.Bits(8)) add_1 (.a(register_1_q), .b(8'h1), .c_i(1'b0), .s(add_1_s));  // open: c_o
  Multiplexer #(.Bits(8)) multiplexer_1 (.sel(str), .in_0(add_1_s), .in_1(Din), .out(D));
endmodule
