// Digital circuit main.dig as structural Verilog
module main (
  input  clk
);

  wire [7:0] pc_1_d, rom_1_d;

  PC pc_1 (.C(clk), .Din({8{1'b0}}), .str(1'b0), .D(pc_1_d));
  ROM #(.AddrBits(8), .Bits(8)) rom_1 (.A(pc_1_d), .sel(1'b1), .D(rom_1_d));
  // Probe on rom_1_d

  // Notes on the sheet:
  //   contents of rom_1 (hex, n*v repeats v):
  //   a00000,140000,e00000,3d0900,2000000,165a0bc00,8000000000,1dcd65000
endmodule
